# Fritzing sketch 555-timer (saved by Fritzing 0.9.4)
circuit board: 8.46667cm x 5.64444cm
breadboards: 1

parts:
  U1 = 555 Timer [package="DIP8 [THT]"]
  R1 = Resistor [tolerance=±5% resistance=220 package="2010 [SMD]"]
  R2 = Resistor [tolerance=±5% resistance=220 package="2010 [SMD]"]
  C1 = Electrolytic Capacitor [capacitance=1000μF package="1010 [SMD, electrolytic]"]
  LED1 = smd LED [color="Red (633nm)" package="0603 [SMD]"]
  R3 = Resistor [tolerance=±5% resistance=220 package=THT]
  C2 = Capacitor [package=cap-pth-small2]
  C3 = Capacitor [package=cap-pth-small2]
  R4 = TRIMPOT [package=trimpot_pth_s3_lock]  # not connected

nets:
  N1: U1.Ground, C1.-, R3.Pin_0, C3.2
  N2: U1.Trigger, U1.Threshold, C1.+
  N3: U1.Output, LED1.anode
  N4: U1.Reset, U1.Vcc_Supply_Voltage, R1.Pin_1, C2.1, C3.1
  N5: U1.Control_Voltage, C2.2
  N6: U1.Discharge, R1.Pin_0, R2.Pin_0
  N7: LED1.cathode, R3.Pin_1

notes:
  PIN8: +5V
  PIN1: ground
  PIN3: output
  PIN4: condensatore messo per avere un'onda migliore
  Condensatore messo per smorzare le transizioni di stato
  PIN4: reset messo a 5V, per evitare che si resetti improvvisamente
  Potenziometro messo per poter decidere sempre a che velocità far andare il clock
